# Fritzing sketch G20_fritzing (saved by Fritzing 0.9.3b)
breadboards: 1

parts:
  Part1 = Itsy Bitsy 32u4 3V @ 8MHz [part_number="Adafruit 3675"]
  J3 = Basic Servo
  Part2 = Adafruit 1.44 inch TFT Breakout [part_number="Adafruit #2088"]
  HC-SR04_Sensor_1 = HC-SR04 Ultrasonic Distance Sensor
  KEYPAD1 = Membrane Matrix Keypad
  R1 = Resistor [tolerance=±5% resistance=2k package="2010 [SMD]"]
  J5 = Piezo Speaker
  R2 = Resistor [tolerance=±5% resistance=2k package="2010 [SMD]"]
  J2 = Basic Servo
  J6 = Basic Servo
  J7 = Basic Servo
  R3 = Resistor [tolerance=±5% resistance=2k package="2010 [SMD]"]
  R4 = Resistor [tolerance=±5% resistance=1k package="2010 [SMD]"]

nets:
  GND: Part1.GND, J3.gnd, Part2.GND, HC-SR04_Sensor_1.GND, KEYPAD1.5, J5.pin1, J2.gnd, J6.gnd, J7.gnd
  N1: Part1.D13, Part1.MOSI, Part2.MOSI, Part2.TFTCS
  N2: Part1.D12, Part2.RESET
  N3: Part1.D10, J5.pin2
  N4: Part1.D9, KEYPAD1.7
  N5: Part1.D7, KEYPAD1.6
  N6: Part1.D5_OUT, J7.pulse
  N7: Part1.SCL, R2.Pin_1
  N8: Part1.SDA, R1.Pin_1
  N9: Part1.D1, J6.pulse
  N10: Part1.MISO, Part2.MISO
  N11: Part1.SCK, Part2.SCK
  N12: Part1.A5, KEYPAD1.1
  N13: Part1.A4, KEYPAD1.2
  N14: Part1.A3, HC-SR04_Sensor_1.TRIG
  N15: Part1.A2, R3.Pin_1, R4.Pin_1
  N16: Part1.A1, KEYPAD1.3
  N17: Part1.A0, KEYPAD1.4
  VCC: Part1.+3V3, J3.vcc, Part2.VIN, Part2.+3V3, HC-SR04_Sensor_1.VCC, J2.vcc, J6.vcc, J7.vcc
  N18: J3.pulse, R1.Pin_0
  N19: HC-SR04_Sensor_1.ECHO, R4.Pin_0
  N20: R2.Pin_0, J2.pulse

custom parts:
  Itsy Bitsy 32u4 3V @ 8MHz: What's smaller than a Feather but larger than a Trinket? It's an Itsy Bitsy! Small, powerful, Arduino-compatible - this microcontroller board is perfect when you want something very compact, but still with a bunch of pins. Itsy Bitsy is only 1.4" long by 0.7" wide, but has 6 power pins, 6 analog & digital pins and 17 digital pins. It packs much of the same capability as an Arduino UNO or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
  Adafruit 1.44 inch TFT Breakout: This lovely little display breakout is the best way to add a small, colorful and bright display to any project. Since the display uses 4-wire SPI to communicate and has its own pixel-addressable frame buffer, it can be used with every kind of microcontroller. Even a very small one with low memory and few pins available! The 1.44" display has 128x128 color pixels. Unlike the low cost "Nokia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
  Membrane Matrix Keypad: Membrane Matrix 3x4 Keypad
